// Logisim project ex5.1.circ as structural Verilog: 2 circuits, main circuit Running_LED
module Running_LED (
  input  [7:0] INITIAL_LED,
  input  RST,
  output [7:0] OUT_LED
);

  wire and_1_out, clock_1_out, counter_1_carry, not_1_out;
  wire [7:0] multiplexer_1_out, register_1_q;

  Clock clock_1 (.out(clock_1_out));
  LED led_1 (.in(OUT_LED[7]));
  Multiplexer #(.width(8)) multiplexer_1 (.in0(OUT_LED), .in1(INITIAL_LED), .out(multiplexer_1_out), .sel(RST));
  and and_1 (and_1_out, clock_1_out, not_1_out);
  Register register_1 (.D(multiplexer_1_out), .clk(and_1_out), .Q(register_1_q));  // open: en, clr
  not not_1 (not_1_out, counter_1_carry);
  LED led_2 (.in(OUT_LED[6]));
  LED led_3 (.in(OUT_LED[5]));
  Counter #(.max('h7)) counter_1 (.carry(counter_1_carry), .clk(and_1_out), .clr(RST));  // open: load, D, count, Q, up
  LED led_4 (.in(OUT_LED[4]));
  rot1 rot1_1 (.in_1(register_1_q), .out_2(OUT_LED));
  LED led_5 (.in(OUT_LED[3]));
  LED led_6 (.in(OUT_LED[2]));
  LED led_7 (.in(OUT_LED[1]));
  LED led_8 (.in(OUT_LED[0]));

  // Notes on the sheet:
  //   PUT CIRCUITS HERE
endmodule

module rot1 (
  input  [7:0] in_1,
  output [7:0] out_2
);


  assign out_2 = {in_1[0], in_1[7:1]};
endmodule
